// Digital circuit handshake.dig as structural Verilog
module handshake (
  input  s_vld,
  input  d_rdy1,
  input  clk,
  input  clr,
  input  d_rdy2,
  output s_rdy,
  output d_vld,
  output d_en,
  output s_en
);

  wire and_2_out, and_3_out, and_5_out, d_ff_1_nq, or_1_out;

  and and_1 (s_en, s_vld, s_rdy);
  or or_1 (or_1_out, and_3_out, s_en);
  and and_2 (and_2_out, or_1_out, ~clr);  // And
  D_FF d_ff_1 (.D(and_2_out), .C(clk), .Q(d_vld), .nQ(d_ff_1_nq));
  or or_2 (s_rdy, and_5_out, d_ff_1_nq);
  and and_3 (and_3_out, d_vld, ~d_en);  // And
  and and_4 (d_en, and_5_out, d_vld);
  and and_5 (and_5_out, d_rdy2, d_rdy1);

  // Other names for the same wires on the sheet: c = clk

  // Notes on the sheet:
  //   rj45Creates
endmodule
