// Digital circuit rjstack.dig as structural Verilog
module rjstack (
  input  clk,
  input  prog_vld,
  output [15:0] ros,
  output [15:0] tos,
  output [11:0] sp,
  output [15:0] nos,
  output [15:0] y,
  output [7:0] i,
  output [7:0] pc,
  output prog_rdy
);

  wire comparator_1_eq, en_fe, halt, handshake_1_d_vld, jump, not_1_out, not_2_out, pop, push, we_i_tos,
       we_nos_tos, we_y_tos;
  wire [7:0] add_1_s, add_2_s, multiplexer_1_out, multiplexer_2_out, npc_q;
  wire [7:6] microcode_d;
  wire [15:0] bitextender_1_out, ir_q, program_d;

  Add #(.Bits(8)) add_1 (.a(npc_q), .b({8{1'b0}}), .c_i(1'b1), .s(add_1_s));  // open: c_o
  Multiplexer #(.Bits(8)) multiplexer_1 (.sel(jump), .in_0(add_1_s), .in_1(add_2_s), .out(multiplexer_1_out));
  Register #(.Bits(8)) npc (.D(multiplexer_1_out), .C(clk), .en(en_fe), .Q(npc_q));
  ROM #(.AddrBits(8), .Bits(16)) \program  (.A(npc_q), .sel(1'b1), .D(program_d));
  Register #(.Bits(8)) u_pc (.D(npc_q), .C(clk), .en(en_fe), .Q(pc));
  Register #(.Bits(16)) ir (.D(program_d), .C(clk), .en(en_fe), .Q(ir_q));
  handshake handshake_1 (
    .s_en(en_fe), .s_vld(prog_vld), .s_rdy(prog_rdy), .clr(jump), .clk(clk), .d_vld(handshake_1_d_vld),
    .d_rdy1(1'b1), .d_rdy2(not_1_out));  // open: d_en
  Add #(.Bits(8)) add_2 (.a(pc), .b(i), .c_i(1'b0), .s(add_2_s));  // open: c_o
  Multiplexer #(.Bits(16)) multiplexer_2 (
    .sel(handshake_1_d_vld), .in_0({16{1'b0}}), .in_1(ir_q), .out({i, multiplexer_2_out}));
  not not_1 (not_1_out, halt);
  BitExtender bitextender_1 (.in(i), .out(bitextender_1_out));
  ROM #(.AddrBits(8), .Bits(8)) microcode (
    .A(multiplexer_2_out), .sel(1'b1), .D({microcode_d, halt, we_y_tos, we_nos_tos, we_i_tos, pop, push}));
  stack stack_1 (
    .clk(clk), .push(push), .pop(pop), .we_itos(we_i_tos), .we_nostos(we_nos_tos), .we_ytos(we_y_tos),
    .i(bitextender_1_out), .y(y), .sp(sp), .ros(ros), .nos(nos), .tos(tos));
  Multiplexer #(.Selector_Bits(2)) multiplexer_3 (
    .sel(microcode_d), .in_0(1'b0), .in_1(1'b1), .in_2(comparator_1_eq), .in_3(not_2_out), .out(jump));
  Add #(.Bits(16)) alu (.a(nos), .b(tos), .c_i(1'b0), .s(y));  // open: c_o
  Comparator #(.Bits(16)) comparator_1 (.a(tos), .b({16{1'b0}}), .eq(comparator_1_eq));  // open: gt, lt
  not not_2 (not_2_out, comparator_1_eq);
  LED u_push (.in(push));
  LED u_pop (.in(pop));
  LED i__gt_tos (.in(we_i_tos));
  LED nos__gt_tos (.in(we_nos_tos));
  LED y__gt_tos (.in(we_y_tos));
  LED u_halt (.in(halt));

  // Other names for the same wires on the sheet: c = clk

  // Notes on the sheet:
  //   clk: Hz: 10
  //   prog_vld: default 1
  //   [05]
  //   rj45Creates
  //   FPGA Stack Machine CPU from Scratch
  //   contents of program (hex, n*v repeats v):
  //   101,201,2,401,2,f901,2,206,8,1,101,3,206,8,f205
  //   contents of microcode (hex, n*v repeats v):
  //   0,5,12,a,9,40,80,c0,20
  //   Pipelined Fetch
endmodule
