// Digital circuit stack.dig as structural Verilog
module stack (
  input  clk,
  input  push,
  input  pop,
  input  we_itos,
  input  we_nostos,
  input  we_ytos,
  input  [15:0] i,
  input  [15:0] y,
  output [11:0] sp,
  output [15:0] ros,
  output [15:0] nos,
  output [15:0] tos
);

  wire or_1_out, or_2_out;
  wire [11:0] add_1_s, multiplexer_1_out, sp_q;
  wire [15:0] multiplexer_2_out, multiplexer_4_out, multiplexer_5_out;

  Multiplexer #(.Bits(12)) multiplexer_1 (.sel(push), .in_0({12{1'b1}}), .in_1(12'h1), .out(multiplexer_1_out));
  Add #(.Bits(12)) add_1 (.a(sp_q), .b(multiplexer_1_out), .c_i(1'b0), .s(add_1_s));  // open: c_o
  or or_1 (or_1_out, push, pop);
  Register #(.Bits(12)) u_sp (.D(add_1_s), .C(clk), .en(or_1_out), .Q(sp_q));
  Multiplexer #(.Bits(16)) multiplexer_2 (.sel(we_itos), .in_0(y), .in_1(i), .out(multiplexer_2_out));
  or or_2 (or_2_out, we_itos, we_nostos, we_ytos);
  Multiplexer #(.Bits(12)) multiplexer_3 (.sel(push), .in_0(add_1_s), .in_1(sp_q), .out(sp));
  Multiplexer #(.Bits(16)) multiplexer_4 (
    .sel(we_nostos), .in_0(multiplexer_2_out), .in_1(nos), .out(multiplexer_4_out));
  Multiplexer #(.Bits(16)) multiplexer_5 (.sel(pop), .in_0(tos), .in_1(ros), .out(multiplexer_5_out));
  Register #(.Bits(16)) u_tos (.D(multiplexer_4_out), .C(clk), .en(or_2_out), .Q(tos));
  Register #(.Bits(16)) u_nos (.D(multiplexer_5_out), .C(clk), .en(or_1_out), .Q(nos));
  RAMDualPort #(.AddrBits(12), .Bits(16)) stack (.A(sp), .Din(nos), .str(push), .C(clk), .ld(1'b1), .D(ros));

  // Other names for the same wires on the sheet: c = clk

  // Notes on the sheet:
  //   rj45Creates
endmodule
